# Fritzing sketch Farm (saved by Fritzing 0.9.9b)

parts:
  Part1 = IFR520 MOS module [package=THT]
  Part2 = Arduino Uno (Rev3)
  Power_RGB1 = Prolight RGB 3 Watt Star
  Power_RGB2 = Prolight RGB 3 Watt Star
  Power_RGB3 = Prolight RGB 3 Watt Star
  Power_RGB4 = Prolight RGB 3 Watt Star
  Power_RGB5 = Prolight RGB 3 Watt Star
  Power_RGB6 = Prolight RGB 3 Watt Star
  Power_RGB7 = Prolight RGB 3 Watt Star
  Power_RGB8 = Prolight RGB 3 Watt Star
  Power_RGB9 = Prolight RGB 3 Watt Star
  Power_RGB10 = Prolight RGB 3 Watt Star
  HLK-PM1 = HLK-PM01

nets:
  N1: Part1.SIG, Part2.D6_PWM
  VCC: Part1.VCC, Part2.5V
  GND: Part1.GND, Part2.GND, HLK-PM1.-Vo
  N2: Part1.V+, Power_RGB1.B+
  N3: Part1.V-, Power_RGB8.B-
  N4: Part1.VIN, HLK-PM1.+Vo
  N5: Power_RGB1.R+, Power_RGB2.B-
  N6: Power_RGB2.R+, Power_RGB3.B-
  N7: Power_RGB3.R+, Power_RGB5.B-
  N8: Power_RGB4.R+, Power_RGB6.B-
  N9: Power_RGB4.B-, Power_RGB5.R+
  N10: Power_RGB6.B+, Power_RGB7.R-
  N11: Power_RGB7.B+, Power_RGB10.R-
  N12: Power_RGB8.R-, Power_RGB9.B+
  N13: Power_RGB9.R-, Power_RGB10.B+
